# Fritzing sketch SmartFarm (saved by Fritzing 0.9.3b)
breadboards: 2

parts:
  Componente1 = Arduino Uno (Rev3) - ICSP
  LED2 = LEDs [package=led10mm]
  R5 = Resistor [tolerance=±5% resistance=220 package=THT]
  R1 = Photocell (LDR) [package=THT]
  R7 = Resistor [tolerance=±5% resistance=220 package=THT]
  Q5 = NPN-Transistor [package="TO92 [THT]"]
  R8 = Resistor [tolerance=±5% resistance=220 package=THT]
  R9 = Photocell (LDR) [package=THT]
  R10 = Resistor [tolerance=±5% resistance=220 package=THT]
  R11 = Resistor [tolerance=±5% resistance=220 package=THT]
  R12 = Photocell (LDR) [package=THT]
  R13 = Resistor [tolerance=±5% resistance=220 package=THT]
  LED5 = LEDs [package=led10mm]
  Q6 = NPN-Transistor [package="TO92 [THT]"]
  LED6 = LEDs [package=led10mm]
  Q7 = NPN-Transistor [package="TO92 [THT]"]
  LED7 = LEDs [package=led10mm]
  Componente2 = Photon
  S1 = Round Pushbutton
  Componente3 = Photon
  DIP-Relay1 = DIP-Relay-D31A [part_number=D31A*]  # not connected
  U1 = RELAY-2 [package=relay-g5v]

nets:
  N1: Componente1.A2, R10.Pin_1
  N2: Componente1.A3, R7.Pin_1
  N3: Componente1.A4/SDA, R13.Pin_1
  N4: Componente1.D9_PWM, U1.1
  N5: Componente1.D10_PWM/SS, R5.Pin_0
  GND: Componente1.GND, Q5.C, Q6.C, Q7.C, Componente2.GND, S1.leg1, Componente3.GND, U1.2
  N6: Componente1.D2, Componente2.TX, Componente3.TX
  N7: Componente1.D3_PWM, Componente2.RX, Componente3.RX
  N8: Componente1.D5_PWM, R8.Pin_0
  N9: Componente1.D6_PWM, R11.Pin_0
  N10: Componente1.D7, S1.leg0
  N11: Componente1.5V, R1.pin_0
  N12: LED2.C, Q5.B
  N13: LED2.A, LED5.A, LED6.A, LED7.A
  N14: R5.Pin_1, Q5.E
  N15: R1.pin_1, R7.Pin_0
  N16: R8.Pin_1, Q6.E
  N17: R9.pin_1, R10.Pin_0
  N18: R11.Pin_1, Q7.E
  N19: R12.pin_1, R13.Pin_0
  N20: LED5.C, Q6.B
  N21: LED6.C, Q7.B
  N22: Componente2.A0, Componente3.A0
  N23: Componente2.A1, Componente3.A1
  N24: Componente2.A2, Componente3.A2
  N25: Componente2.A3, Componente3.A3
  N26: Componente2.A4, Componente3.A4
  N27: Componente2.A5, Componente3.A5
  N28: Componente2.DAC, Componente3.DAC
  N29: Componente2.WKP, Componente3.WKP
  VIN: Componente2.VIN, Componente3.VIN
  N30: Componente2.D0, Componente3.D0
  N31: Componente2.D1, Componente3.D1
  N32: Componente2.D2, Componente3.D2
  N33: Componente2.D3, Componente3.D3
  N34: Componente2.D4, Componente3.D4
  N35: Componente2.D5, Componente3.D5
  N36: Componente2.D6, Componente3.D6
  N37: Componente2.D7, Componente3.D7
  N38: Componente2.VBAT, Componente3.VBAT
  N39: Componente2.RST, Componente3.RST
  3V3: Componente2.3V3, Componente3.3V3

notes:
  Fuente 12V
